# Fritzing sketch Rover1.0 (saved by Fritzing 0.9.3b)
breadboards: 1

parts:
  Part1 = Arduino Fio (Funnel I/O)
  Part2 = Arduino Uno (Rev3)
  Part3 = 9 Degrees of Freedom - Sensor Stick

nets:
  GND: Part1.GND, Part2.GND, Part3.SCL
  N1: Part1.D2, Part2.A5/SCL, Part3.GND
  N2: Part1.D3_PWM, Part2.A4/SDA, Part3.VCC
  VCC: Part1.VCC, Part2.3V3, Part3.SDA
